// Logisim project theremin_toplevel.circ as structural Verilog: 1 circuit, main circuit theremin_toplevel
module theremin_toplevel (
  input  clk,
  input  PMOD_0_1,
  input  PMOD_1_1,
  input  [7:0] switches,
  output PMOD_0_0,
  output PMOD_0_2,
  output PMOD_1_0,
  output PMOD_1_2,
  output [6:0] cathodes,
  output anode0,
  output anode1,
  output anode2,
  output anode3
);

  wire not_1_out, not_2_out, tlc548_1_cs, tlc548_1_io_clock, tlc548_2_cs, tlc548_2_io_clock;
  wire [7:0] CPU_Interface_1_p6, CPU_Interface_1_p7, tlc548_1_value, tlc548_2_value;

  not not_1 (not_1_out, PMOD_0_1);
  not not_2 (not_2_out, PMOD_1_1);
  tlc548 tlc548_1 (
    .clk(clk), .data_in(not_1_out), .cs(tlc548_1_cs), .io_clock(tlc548_1_io_clock), .value(tlc548_1_value));
  not not_3 (PMOD_0_0, tlc548_1_cs);
  not not_4 (PMOD_0_2, tlc548_1_io_clock);
  tlc548 tlc548_2 (
    .clk(clk), .data_in(not_2_out), .cs(tlc548_2_cs), .io_clock(tlc548_2_io_clock), .value(tlc548_2_value));
  not not_5 (PMOD_1_0, tlc548_2_cs);
  not not_6 (PMOD_1_2, tlc548_2_io_clock);
  // CPU_Interface CPU_Interface_1: pin names not known; wires that end beside it: clk, tlc548_1_value, 1'b1, tlc548_2_value, 1'b1, CPU_Interface_1_p6, CPU_Interface_1_p7
  bytes_display bytes_debug (
    .octet1(CPU_Interface_1_p6), .octet1_enable(1'b1), .octet2(CPU_Interface_1_p7), .octet2_enable(1'b1),
    .reset(1'b0), .clk(clk), .cathodes(cathodes), .anode0(anode0), .anode1(anode1), .anode2(anode2),
    .anode3(anode3));
endmodule
